# Fritzing sketch littebotbut (saved by Fritzing 0.9.9b)

parts:
  Amica_NodeMCU = Amica NodeMCU DevKit 1.0
  switch = Pushbutton [package="[THT]"]
  R = Resistor [tolerance=±5% power=0.25 resistance=10k package=THT]

nets:
  N1: Amica_NodeMCU.pin2, Amica_NodeMCU.pin_9, R.Pin_0
  N2: Amica_NodeMCU.pin8, switch.Pin_1, switch.Pin_2, R.Pin_1
  N3: Amica_NodeMCU.pin_10, switch.Pin_3, switch.Pin_4

custom parts:
  Amica NodeMCU DevKit 1.0: Amica NodeMCU DEVKIT 1.0 Development Kit based on ESP8266 ESP-12E, integating GPIO, PWM, IIC, 1-Wire and ADC all in one board.
